# Fritzing sketch battery-toolbox (saved by Fritzing 0.9.6b)
breadboards: 1

parts:
  U1 = LCD-16X2 [package=lcd-16x2_noholes]
  R3 = Resistor [tolerance=±5% power=0.25 resistance=220 package=THT]
  R4 = Trimmer Potentiometer [maximum_resistance=25kΩ package=THT]
  U4_(Rotary_encoder) = ENCODER-QUADRATURE [package=encoder-16mm-quad]
  C3 = Ceramic Capacitor [capacitance=100nF voltage=35V package="100 mil [THT, multilayer]"]
  C4 = Ceramic Capacitor [capacitance=100nF voltage=35V package="100 mil [THT, multilayer]"]
  S1_(Rotary_Push)1 = Pushbutton [package="[THT]"]
  C5 = Ceramic Capacitor [capacitance=100nF voltage=35V package="100 mil [THT, multilayer]"]
  R8 = Resistor [tolerance=±5% power=0.25 resistance=50k package=THT]
  R9 = Resistor [tolerance=±5% power=0.25 resistance=22 package=THT]
  D2 = Zener Diode [breakdown_voltage=4.7V part_number=1N4732A package="Melf DO-213 AB [SMD]"]
  Part2 = Arduino Uno (Rev3)
  U5 = ACS712 [package=so08]
  V4 = DC Power [voltage=12V part_number=Battery]
  Q1 = Basic FET N-Channel [part_number=D472 package="D2Pak [SMD]"]
  Fuse1 = Fuse with Handler [part_number=Htc-15A]
  C6 = Ceramic Capacitor [capacitance=1nF voltage=35V package="100 mil [THT, multilayer]"]
  R10 = Resistor [tolerance=±5% power=0.25 resistance=1.8k package=THT]
  R11 = Resistor [tolerance=±5% power=0.25 resistance=47k package=THT]
  C7 = Ceramic Capacitor [capacitance=100nF voltage=35V package="100 mil [THT, multilayer]"]
  C8 = Ceramic Capacitor [capacitance=100nF voltage=35V package="100 mil [THT, multilayer]"]
  R13 = Resistor [tolerance=±1% power=0.25W resistance=13k package=THT]
  R14 = Resistor [tolerance=±1% power=0.25 resistance=44.2k package=THT]
  C11 = Electrolytic Capacitor [capacitance=10µF voltage=6.3V package="100 mil [THT, electrolytic]"]
  R16 = Temperature Sensor (Thermistor) [thermistor_type=NTC part_number="B3950 (100K)" package=THT]
  R17 = Resistor [tolerance=±5% power=0.25 resistance=4.7k package=THT]
  C13 = Electrolytic Capacitor [capacitance=1mF voltage=6.3V package="100 mil [THT, electrolytic]"]
  S1 = SWITCH-DPDT [package=ayz0202]
  R18 = Resistor [tolerance=±5% power=0.25 resistance=1k package=THT]
  J1 = Piezo Speaker
  R19 = Resistor [tolerance=±5% power=0.25 resistance=1.8k package=THT]
  R20 = Resistor [tolerance=±1% power=0.25W resistance=13k package=THT]
  R22 = Resistor [tolerance=±1% power=0.25 resistance=44.2k package=THT]
  J2 = Screw terminal - 2 pins [part_number="Charging Supply" package=THT]
  J3 = Screw terminal - 2 pins [part_number="+12V Main Supply" package=THT]
  C14 = Ceramic Capacitor [capacitance=100nF voltage=35V package="100 mil [THT, multilayer]"]

nets:
  GND: U1.VSS, U1.R_W, R4.leg2, U4_(Rotary_encoder).C, C3.0, C4.0, S1_(Rotary_Push)1.Pin_3, S1_(Rotary_Push)1.Pin_4, C5.0, D2.anode, Part2.GND, C11.-, R17.Pin_0, C13.-, J1.pin1
  5V: U1.VDD, U1.K, R3.Pin_1, R4.leg1, R8.Pin_1, R9.Pin_1, Part2.5V, U5.VCC, C8.1, C13.+
  N1: U1.VO, R4.wiper
  N2: U1.RS, Part2.D13/SCK
  N3: U1.E, Part2.D12/MISO
  N4: U1.DB4, Part2.D8
  N5: U1.DB5, Part2.D7
  N6: U1.DB6, Part2.D5_PWM
  N7: U1.DB7, Part2.D4
  N8: U1.A, R3.Pin_0
  N9: U4_(Rotary_encoder).A, C3.1, Part2.D2
  N10: U4_(Rotary_encoder).B, C4.1, Part2.D3_PWM
  N11: S1_(Rotary_Push)1.Pin_1, S1_(Rotary_Push)1.Pin_2, C5.1, R8.Pin_0, Part2.A4/SDA
  N12: R9.Pin_0, D2.cathode, Part2.AREF, C11.+, R16.pin_1
  N13: Part2.A0, R13.Pin_0, R14.Pin_1
  N14: Part2.A1, R10.Pin_1, R11.Pin_1, C7.1
  N15: Part2.A2, R16.pin_0, R17.Pin_1
  N16: Part2.A5/SCL, R20.Pin_0, R22.Pin_1
  N17: Part2.D9_PWM, R18.Pin_1
  N18: Part2.D6_PWM, R19.Pin_0
  N19: Part2.VIN, J3.pin1, C14.1
  N20: U5.IP+, Fuse1.Connector1, R14.Pin_0
  N21: U5.IP-, Q1.drain
  N22: U5.GND, Q1.source, C6.0, R11.Pin_0, C7.0, C8.0, R13.Pin_1, S1.6, R20.Pin_1, J2.pin2, J3.pin2, C14.0
  N23: U5.FILT, C6.1
  N24: U5.VOUT, R10.Pin_0
  N25: V4.V+, S1.2
  N26: V4.V-, S1.5
  N27: Q1.Gate, R18.Pin_0
  N28: Fuse1.Connector2, S1.3, S1.4
  N29: S1.1, R22.Pin_0, J2.pin1
  N30: J1.pin2, R19.Pin_1
